# Fritzing sketch esp1&2 (saved by Fritzing 0.9.10b)
breadboards: 1

parts:
  Mod2 = Amica NodeMCU DEVKIT 1.0
  Part1 = RFID-RC522-v2
  Keypad4x1 = Keypad Membran 4x4
  PIR2 = PIR sensor
  Mod3 = Amica NodeMCU DEVKIT 1.0
  Part3 = LCD1602-I2C

nets:
  3.3V: Mod2.pin1, Mod2.pin_10, Mod2.pin_26, Part1.RST, Part1.3.3V, PIR2.VDD, Part3.VCC
  GND: Mod2.pin2, Mod2.pin_9, Mod2.pin_25, Mod2.pin_29, Part1.GND, Part3.GND
  N1: Mod2.pin6, Part3.SCL
  N2: Mod2.pin7, Part3.SDA
  N3: Mod2.pin8, PIR2.SIG
  N4: Mod2.pin_11, Part1.MISO
  N5: Mod2.pin_12, Part1.MOSI
  N6: Mod2.pin_13, Part1.SCK
  N7: Mod2.pin_14, Part1.SDA
  N8: Keypad4x1.Pin1, Mod3.pin_15
  N9: Keypad4x1.Pin2, Mod3.pin_14
  N10: Keypad4x1.Pin3, Mod3.pin_13
  N11: Keypad4x1.Pin4, Mod3.pin_12
  N12: Keypad4x1.Pin5, Mod3.pin_11
  N13: Keypad4x1.Pin6, Mod3.pin8
  N14: Keypad4x1.Pin7, Mod3.pin7
  N15: Keypad4x1.Pin8, Mod3.pin6
  N16: Mod3.pin1, Mod3.pin_10, Mod3.pin_26
  N17: Mod3.pin2, Mod3.pin_9, Mod3.pin_25, Mod3.pin_29

custom parts:
  RFID-RC522-v2: A simple China made RFID-RC522 Reader; do check the pin labels, as this is a MFRC522 based clone.
  Keypad Membran 4x4: Membrane Keypad 4x4 Matrix
  LCD1602-I2C: A standard character display, usually with 2x16 characters. Comes in many colors with LCM1602 IIC attached.
