# Fritzing sketch esp3 (saved by Fritzing 0.9.10b)
breadboards: 1

parts:
  Mod1 = Amica NodeMCU DEVKIT 1.0
  J1 = Basic Servo
  LED2 = RGB LED (com. anode, rbg) [package="5 mm [THT]"]
  buz1 = Piezo Buzzer
  R1 = Resistor [tolerance=±5% resistance=220 package="2512 [SMD]"]

nets:
  N1: Mod1.pin1, Mod1.pin_10, Mod1.pin_26, J1.vcc
  N2: Mod1.pin2, Mod1.pin_9, Mod1.pin_25, Mod1.pin_29, J1.gnd, buz1.pin_2, R1.Pin_0
  N3: Mod1.pin6, J1.pulse
  N4: Mod1.pin_11, buz1.pin_1
  N5: Mod1.pin_13, LED2.red_cathode
  N6: Mod1.pin_14, LED2.green_cathode
  N7: LED2.blue_cathode, R1.Pin_1

custom parts:
  Piezo Buzzer: Part from https://www.nutsvolts.com/magazine/article/november2012_SmileysWorkshop. Breadboard and icon images modified to be 0.3" in spacing and be more similar to the actual physical part.
