# Fritzing sketch lcd_servo (saved by Fritzing 0.9.10b)
breadboards: 1

parts:
  Mod1 = Amica NodeMCU DEVKIT 1.0
  Part2 = LCD1602-I2C
  J1 = Basic Servo

nets:
  VCC: Mod1.pin1, Mod1.pin2, Mod1.pin_9, Mod1.pin_10, Mod1.pin_25, Mod1.pin_26, Mod1.pin_29, Part2.VCC, J1.vcc
  N1: Mod1.pin6, J1.pulse
  N2: Mod1.pin7, Part2.SDA
  N3: Mod1.pin8, Part2.SCL
  GND: Part2.GND, J1.gnd

custom parts:
  LCD1602-I2C: A standard character display, usually with 2x16 characters. Comes in many colors with LCM1602 IIC attached.
